// Logisim project psMCU.circ as structural Verilog: 24 circuits, main circuit main
module FullAdder (
  input  A,
  input  B,
  input  Cin,
  output Out,
  output Cout
);

  wire and_1_out, and_2_out, xor_1_out;

  xor xor_1 (xor_1_out, A, B);
  xor xor_2 (Out, xor_1_out, Cin);
  and and_1 (and_1_out, xor_1_out, Cin);
  and and_2 (and_2_out, B, A);
  or or_1 (Cout, and_1_out, and_2_out);
endmodule

module Complementer (
  input  [7:0] IN,
  output [7:0] OUT
);

  wire and_1_out, and_2_out, and_3_out, and_4_out, and_5_out, and_6_out, and_7_out;
  wire [7:0] not_1_out;

  and and_1 (and_1_out, and_2_out, not_1_out[6]);
  xor xor_1 (OUT[7], not_1_out[7], and_1_out);
  xor xor_2 (OUT[6], not_1_out[6], and_2_out);
  and and_2 (and_2_out, and_3_out, not_1_out[5]);
  xor xor_3 (OUT[5], not_1_out[5], and_3_out);
  assign not_1_out = ~IN;  // NOT_Gate not_1, 8 bits wide
  and and_3 (and_3_out, and_4_out, not_1_out[4]);
  xor xor_4 (OUT[4], not_1_out[4], and_4_out);
  and and_4 (and_4_out, and_5_out, not_1_out[3]);
  xor xor_5 (OUT[3], not_1_out[3], and_5_out);
  and and_5 (and_5_out, and_6_out, not_1_out[2]);
  and and_6 (and_6_out, and_7_out, not_1_out[1]);
  xor xor_6 (OUT[2], not_1_out[2], and_6_out);
  xor xor_7 (OUT[1], not_1_out[1], and_7_out);
  and and_7 (and_7_out, 1'b1, not_1_out[0]);
  xor xor_8 (OUT[0], not_1_out[0], 1'b1);

  // Notes on the sheet:
  //   LSB Could be just one not gate, if it reduces chip count
endmodule

module BarrelShifter (
  input  OE,
  input  [7:0] Register_A,
  input  Shift_In,
  input  R,
  input  [7:0] Operand_B,
  output [7:0] DBus_OUT
);

  wire multiplexer_1_out, multiplexer_2_out, multiplexer_3_out, multiplexer_4_out, multiplexer_6_out,
       multiplexer_7_out, multiplexer_8_out, multiplexer_9_out, multiplexer_10_out, multiplexer_12_out,
       multiplexer_13_out, multiplexer_14_out, multiplexer_16_out, multiplexer_17_out, multiplexer_18_out,
       multiplexer_19_out, multiplexer_21_out, multiplexer_22_out, multiplexer_23_out, multiplexer_24_out,
       multiplexer_26_out, multiplexer_27_out, multiplexer_28_out, multiplexer_29_out, multiplexer_31_out,
       multiplexer_32_out, multiplexer_33_out, multiplexer_34_out, multiplexer_36_out, multiplexer_37_out,
       multiplexer_38_out, multiplexer_39_out;
  wire [7:0] multiplexer_40_out;

  Multiplexer #(.enable("false")) multiplexer_1 (
    .in0(Register_A[7]), .in1(Register_A[0]), .out(multiplexer_1_out), .sel(R));
  Multiplexer #(.enable("false")) multiplexer_2 (
    .in0(multiplexer_1_out), .in1(multiplexer_6_out), .out(multiplexer_2_out), .sel(Operand_B[0]));
  Multiplexer #(.enable("false")) multiplexer_3 (
    .in0(multiplexer_2_out), .in1(multiplexer_12_out), .out(multiplexer_3_out), .sel(Operand_B[1]));
  Multiplexer #(.enable("false")) multiplexer_4 (
    .in0(multiplexer_3_out), .in1(multiplexer_23_out), .out(multiplexer_4_out), .sel(Operand_B[2]));
  Multiplexer #(.enable("false")) multiplexer_5 (
    .in0(multiplexer_4_out), .in1(multiplexer_39_out), .out(multiplexer_40_out[7]), .sel(R));
  Multiplexer #(.enable("false")) multiplexer_6 (
    .in0(Register_A[6]), .in1(Register_A[1]), .out(multiplexer_6_out), .sel(R));
  Multiplexer #(.enable("false")) multiplexer_7 (
    .in0(multiplexer_6_out), .in1(multiplexer_10_out), .out(multiplexer_7_out), .sel(Operand_B[0]));
  Multiplexer #(.enable("false")) multiplexer_8 (
    .in0(multiplexer_7_out), .in1(multiplexer_17_out), .out(multiplexer_8_out), .sel(Operand_B[1]));
  Multiplexer #(.enable("false")) multiplexer_9 (
    .in0(multiplexer_8_out), .in1(multiplexer_28_out), .out(multiplexer_9_out), .sel(Operand_B[2]));
  Multiplexer #(.enable("false")) multiplexer_10 (
    .in0(Register_A[5]), .in1(Register_A[2]), .out(multiplexer_10_out), .sel(R));
  Multiplexer #(.enable("false")) multiplexer_11 (
    .in0(multiplexer_9_out), .in1(multiplexer_34_out), .out(multiplexer_40_out[6]), .sel(R));
  assign DBus_OUT = OE ? multiplexer_40_out : 8'bz;  // Controlled_Buffer controlled_buffer_1
  Multiplexer #(.enable("false")) multiplexer_12 (
    .in0(multiplexer_10_out), .in1(multiplexer_16_out), .out(multiplexer_12_out), .sel(Operand_B[0]));
  Multiplexer #(.enable("false")) multiplexer_13 (
    .in0(multiplexer_12_out), .in1(multiplexer_22_out), .out(multiplexer_13_out), .sel(Operand_B[1]));
  Multiplexer #(.enable("false")) multiplexer_14 (
    .in0(multiplexer_13_out), .in1(multiplexer_33_out), .out(multiplexer_14_out), .sel(Operand_B[2]));
  Multiplexer #(.enable("false")) multiplexer_15 (
    .in0(multiplexer_14_out), .in1(multiplexer_29_out), .out(multiplexer_40_out[5]), .sel(R));
  Multiplexer #(.enable("false")) multiplexer_16 (
    .in0(Register_A[4]), .in1(Register_A[3]), .out(multiplexer_16_out), .sel(R));
  Multiplexer #(.enable("false")) multiplexer_17 (
    .in0(multiplexer_16_out), .in1(multiplexer_21_out), .out(multiplexer_17_out), .sel(Operand_B[0]));
  Multiplexer #(.enable("false")) multiplexer_18 (
    .in0(multiplexer_17_out), .in1(multiplexer_27_out), .out(multiplexer_18_out), .sel(Operand_B[1]));
  Multiplexer #(.enable("false")) multiplexer_19 (
    .in0(multiplexer_18_out), .in1(multiplexer_38_out), .out(multiplexer_19_out), .sel(Operand_B[2]));
  Multiplexer #(.enable("false")) multiplexer_20 (
    .in0(multiplexer_19_out), .in1(multiplexer_24_out), .out(multiplexer_40_out[4]), .sel(R));
  Multiplexer #(.enable("false")) multiplexer_21 (
    .in0(Register_A[3]), .in1(Register_A[4]), .out(multiplexer_21_out), .sel(R));
  Multiplexer #(.enable("false")) multiplexer_22 (
    .in0(multiplexer_21_out), .in1(multiplexer_26_out), .out(multiplexer_22_out), .sel(Operand_B[0]));
  Multiplexer #(.enable("false")) multiplexer_23 (
    .in0(multiplexer_22_out), .in1(multiplexer_32_out), .out(multiplexer_23_out), .sel(Operand_B[1]));
  Multiplexer #(.enable("false")) multiplexer_24 (
    .in0(multiplexer_23_out), .in1(Shift_In), .out(multiplexer_24_out), .sel(Operand_B[2]));
  Multiplexer #(.enable("false")) multiplexer_25 (
    .in0(multiplexer_24_out), .in1(multiplexer_19_out), .out(multiplexer_40_out[3]), .sel(R));
  Multiplexer #(.enable("false")) multiplexer_26 (
    .in0(Register_A[2]), .in1(Register_A[5]), .out(multiplexer_26_out), .sel(R));
  Multiplexer #(.enable("false")) multiplexer_27 (
    .in0(multiplexer_26_out), .in1(multiplexer_31_out), .out(multiplexer_27_out), .sel(Operand_B[0]));
  Multiplexer #(.enable("false")) multiplexer_28 (
    .in0(multiplexer_27_out), .in1(multiplexer_37_out), .out(multiplexer_28_out), .sel(Operand_B[1]));
  Multiplexer #(.enable("false")) multiplexer_29 (
    .in0(multiplexer_28_out), .in1(Shift_In), .out(multiplexer_29_out), .sel(Operand_B[2]));
  Multiplexer #(.enable("false")) multiplexer_30 (
    .in0(multiplexer_29_out), .in1(multiplexer_14_out), .out(multiplexer_40_out[2]), .sel(R));
  Multiplexer #(.enable("false")) multiplexer_31 (
    .in0(Register_A[1]), .in1(Register_A[6]), .out(multiplexer_31_out), .sel(R));
  Multiplexer #(.enable("false")) multiplexer_32 (
    .in0(multiplexer_31_out), .in1(multiplexer_36_out), .out(multiplexer_32_out), .sel(Operand_B[0]));
  Multiplexer #(.enable("false")) multiplexer_33 (
    .in0(multiplexer_32_out), .in1(Shift_In), .out(multiplexer_33_out), .sel(Operand_B[1]));
  Multiplexer #(.enable("false")) multiplexer_34 (
    .in0(multiplexer_33_out), .in1(Shift_In), .out(multiplexer_34_out), .sel(Operand_B[2]));
  Multiplexer #(.enable("false")) multiplexer_35 (
    .in0(multiplexer_34_out), .in1(multiplexer_9_out), .out(multiplexer_40_out[1]), .sel(R));
  Multiplexer #(.enable("false")) multiplexer_36 (
    .in0(Register_A[0]), .in1(Register_A[7]), .out(multiplexer_36_out), .sel(R));
  Multiplexer #(.enable("false")) multiplexer_37 (
    .in0(multiplexer_36_out), .in1(Shift_In), .out(multiplexer_37_out), .sel(Operand_B[0]));
  Multiplexer #(.enable("false")) multiplexer_38 (
    .in0(multiplexer_37_out), .in1(Shift_In), .out(multiplexer_38_out), .sel(Operand_B[1]));
  Multiplexer #(.enable("false")) multiplexer_39 (
    .in0(multiplexer_38_out), .in1(Shift_In), .out(multiplexer_39_out), .sel(Operand_B[2]));
  Multiplexer #(.enable("false")) multiplexer_40 (
    .in0(multiplexer_39_out), .in1(multiplexer_4_out), .out(multiplexer_40_out[0]), .sel(R));
endmodule

module ALU (
  input  [7:0] Register_A,
  input  [7:0] Operand_B,
  input  [7:0] RegB_Komplement,
  input  Do_B_Komp,
  input  OE,
  output [7:0] DBus_OUT,
  output HBorrow,
  output Borrow,
  output Carry,
  output Borrow_2
);

  wire fulladder_1_cout, fulladder_2_cout, fulladder_3_cout, fulladder_5_cout, fulladder_6_cout,
       fulladder_7_cout;
  wire [7:0] fulladder_1_out, multiplexer_1_out;

  Multiplexer #(.width(8), .enable("false")) multiplexer_1 (
    .in0(Operand_B), .in1(RegB_Komplement), .out(multiplexer_1_out), .sel(Do_B_Komp));
  FullAdder fulladder_1 (
    .A(Register_A[0]), .B(multiplexer_1_out[0]), .Cin(1'b0), .Out(fulladder_1_out[0]), .Cout(fulladder_1_cout));
  FullAdder fulladder_2 (
    .A(Register_A[1]), .B(multiplexer_1_out[1]), .Cin(fulladder_1_cout), .Out(fulladder_1_out[1]),
    .Cout(fulladder_2_cout));
  FullAdder fulladder_3 (
    .A(Register_A[2]), .B(multiplexer_1_out[2]), .Cin(fulladder_2_cout), .Out(fulladder_1_out[2]),
    .Cout(fulladder_3_cout));
  FullAdder fulladder_4 (
    .A(Register_A[3]), .B(multiplexer_1_out[3]), .Cin(fulladder_3_cout), .Out(fulladder_1_out[3]),
    .Cout(HBorrow));
  FullAdder fulladder_5 (
    .A(Register_A[4]), .B(multiplexer_1_out[4]), .Cin(HBorrow), .Out(fulladder_1_out[4]),
    .Cout(fulladder_5_cout));
  FullAdder fulladder_6 (
    .A(Register_A[5]), .B(multiplexer_1_out[5]), .Cin(fulladder_5_cout), .Out(fulladder_1_out[5]),
    .Cout(fulladder_6_cout));
  FullAdder fulladder_7 (
    .A(Register_A[6]), .B(multiplexer_1_out[6]), .Cin(fulladder_6_cout), .Out(fulladder_1_out[6]),
    .Cout(fulladder_7_cout));
  FullAdder fulladder_8 (
    .A(Register_A[7]), .B(multiplexer_1_out[7]), .Cin(fulladder_7_cout), .Out(fulladder_1_out[7]),
    .Cout(Carry));
  not not_1 (Borrow_2, Carry);
  assign DBus_OUT = OE ? fulladder_1_out : 8'bz;  // Controlled_Buffer controlled_buffer_1
  not not_2 (Borrow, HBorrow);
endmodule

module Temp_Reg (
  input  [7:0] DBUS_In,
  input  LATCH_L,
  input  LATCH_H,
  input  CLK,
  input  RESET,
  input  OE_ADR,
  input  OE_DATAL,
  output [7:0] DBG_L,
  output [7:0] DBUS_Out,
  output [13:0] ROMABus_Out,
  output [7:0] DBG_H
);

  Register register_1 (.D(DBUS_In), .en(LATCH_L), .Q(DBG_L), .clk(CLK), .clr(RESET));
  Register register_2 (.D(DBUS_In), .en(LATCH_H), .Q(DBG_H), .clk(CLK), .clr(RESET));
  assign DBUS_Out = OE_DATAL ? DBG_L : 8'bz;  // Controlled_Buffer controlled_buffer_1
  assign ROMABus_Out = OE_ADR ? {DBG_H[5:0], DBG_L} : 14'bz;  // Controlled_Buffer controlled_buffer_2
endmodule

module Logic (
  input  [1:0] DUAL_OP_CODE,
  input  [7:0] Register_A,
  input  [7:0] Operand_B,
  input  [7:0] Register_B,
  input  COMP,
  input  NOT,
  input  DUAL_OP_OE,
  output [7:0] Register_B_Complement,
  output [7:0] DBus_Out
);

  wire and_1_out, and_2_out, and_3_out, and_5_out, and_6_out, and_7_out, not_1_out, not_2_out;
  wire [7:0] and_4_out, not_3_out, or_1_out, xor_1_out;

  and and_1 (and_1_out, not_1_out, not_2_out);
  not not_1 (not_1_out, DUAL_OP_CODE[1]);
  not not_2 (not_2_out, DUAL_OP_CODE[0]);
  and and_2 (and_2_out, DUAL_OP_CODE[1], not_2_out);
  and and_3 (and_3_out, not_1_out, DUAL_OP_CODE[0]);
  assign not_3_out = ~Register_A;  // NOT_Gate not_3, 8 bits wide
  assign DBus_Out = NOT ? not_3_out : 8'bz;  // Controlled_Buffer controlled_buffer_1
  assign and_4_out = Register_A & Operand_B;  // AND_Gate and_4, 8 bits wide
  and and_5 (and_5_out, and_1_out, DUAL_OP_OE);
  assign DBus_Out = and_5_out ? and_4_out : 8'bz;  // Controlled_Buffer controlled_buffer_2
  and and_6 (and_6_out, and_3_out, DUAL_OP_OE);
  assign or_1_out = Register_A | Operand_B;  // OR_Gate or_1, 8 bits wide
  assign DBus_Out = and_6_out ? or_1_out : 8'bz;  // Controlled_Buffer controlled_buffer_3
  assign xor_1_out = Register_A ^ Operand_B;  // XOR_Gate xor_1, 8 bits wide
  and and_7 (and_7_out, and_2_out, DUAL_OP_OE);
  assign DBus_Out = and_7_out ? xor_1_out : 8'bz;  // Controlled_Buffer controlled_buffer_4
  Complementer complementer_1 (.IN(Register_B), .OUT(Register_B_Complement));
  assign DBus_Out = COMP ? Register_B_Complement : 8'bz;  // Controlled_Buffer controlled_buffer_5
endmodule

module Inst_Reg (
  input  [15:0] NextInst_Input,
  input  LATCH_EN,
  input  CLK,
  input  RESET,
  output [15:0] Inst_Output
);

  Register #(.width(16)) register_1 (.D(NextInst_Input), .en(LATCH_EN), .Q(Inst_Output), .clk(CLK), .clr(RESET));
endmodule

module ROM (
  input  [13:0] PC_VAL_IN,
  output [15:0] NextInst_OUT
);

  ROM_part #(.addrWidth(14), .dataWidth(16)) rom_1 (.addr(PC_VAL_IN), .data(NextInst_OUT), .sel(1'b1));

  // Notes on the sheet:
  //   contents of rom_1 (hex, n*v repeats v):
  //   1c00 2400 1c01 2401 1c02 2402 1c03 2403 1c04 2404 1c05 2405 1c06 2406 1c07 2407 1c08 2408 1c09 2409
  //   1c0a 240a 1c0b 240b 1c0c 240c 1c0d 240d 1c0e 240e 1c0f 240f 1c10 2410 1c11 2411 1c12 2412 1c13 2413
  //   1c14 2414 1c15 2415 1c16 2416 1c17 2417 1c18 2418 1c19 2419 1c1a 241a 1c1b 241b 1c1c 241c 1c1d 241d
  //   1c1e 241e 1c1f 241f 1c20 2420 1c21 2421 1c22 2422 1c23 2423 1c24 2424 1c25 2425 1c26 2426 1c27 2427
  //   1c28 2428 1c29 2429 1c2a 242a 1c2b 242b 1c2c 242c 1c2d 242d 1c2e 242e 1c2f 242f 1c30 2430 1c31 2431
  //   1c32 2432 1c33 2433 1c34 2434 1c35 2435 1c36 2436 1c37 2437 1c38 2438 1c39 2439 1c3a 243a 1c3b 243b
  //   1c3c 243c 1c3d 243d 1c3e 243e 1c3f 243f 1c40 2440 1c41 2441 1c42 2442 1c43 2443 1c44 2444 1c45 2445
  //   1c46 2446 1c47 2447 1c48 2448 1c49 2449 1c4a 244a 1c4b 244b 1c4c 244c 1c4d 244d 1c4e 244e 1c4f 244f
  //   1c50 2450 1c51 2451 1c52 2452 1c53 2453 1c54 2454 1c55 2455 1c56 2456 1c57 2457 1c58 2458 1c59 2459
  //   1c5a 245a 1c5b 245b 1c5c 245c 1c5d 245d 1c5e 245e 1c5f 245f 1c60 2460 1c61 2461 1c62 2462 1c63 2463
  //   1c64 2464 1c65 2465 1c66 2466 1c67 2467 1c68 2468 1c69 2469 1c6a 246a 1c6b 246b 1c6c 246c 1c6d 246d
  //   1c6e 246e 1c6f 246f 1c70 2470 1c71 2471 1c72 2472 1c73 2473 1c74 2474 1c75 2475 1c76 2476 1c77 2477
  //   1c78 2478 1c79 2479 1c7a 247a 1c7b 247b 1c7c 247c 1c7d 247d 1c7e 247e 1c7f 247f 1c80 2480 1c81 2481
  //   1c82 2482 1c83 2483 1c84 2484 1c85 2485 1c86 2486 1c87 2487 1c88 2488 1c89 2489 1c8a 248a 1c8b 248b
  //   1c8c 248c 1c8d 248d 1c8e 248e 1c8f 248f 1c90 2490 1c91 2491 1c92 2492 1c93 2493 1c94 2494 1c95 2495
  //   1c96 2496 1c97 2497 1c98 2498 1c99 2499 1c9a 249a 1c9b 249b 1c9c 249c 1c9d 249d 1c9e 249e 1c9f 249f
  //   1ca0 24a0 1ca1 24a1 1ca2 24a2 1ca3 24a3 1ca4 24a4 1ca5 24a5 1ca6 24a6 1ca7 24a7 1ca8 24a8 1ca9 24a9
  //   1caa 24aa 1cab 24ab 1cac 24ac 1cad 24ad 1cae 24ae 1caf 24af 1cb0 24b0 1cb1 24b1 1cb2 24b2 1cb3 24b3
  //   1cb4 24b4 1cb5 24b5 1cb6 24b6 1cb7 24b7 1cb8 24b8 1cb9 24b9 1cba 24ba 1cbb 24bb 1cbc 24bc 1cbd 24bd
  //   1cbe 24be 1cbf 24bf 1cc0 24c0 1cc1 24c1 1cc2 24c2 1cc3 24c3 1cc4 24c4 1cc5 24c5 1cc6 24c6 1cc7 24c7
  //   1cc8 24c8 1cc9 24c9 1cca 24ca 1ccb 24cb 1ccc 24cc 1ccd 24cd 1cce 24ce 1ccf 24cf 1cd0 24d0 1cd1 24d1
  //   1cd2 24d2 1cd3 24d3 1cd4 24d4 1cd5 24d5 1cd6 24d6 1cd7 24d7 1cd8 24d8 1cd9 24d9 1cda 24da 1cdb 24db
  //   1cdc 24dc 1cdd 24dd 1cde 24de 1cdf 24df 1ce0 24e0 1ce1 24e1 1ce2 24e2 1ce3 24e3 1ce4 24e4 1ce5 24e5
  //   1ce6 24e6 1ce7 24e7 1ce8 24e8 1ce9 24e9 1cea 24ea 1ceb 24eb 1cec 24ec 1ced 24ed 1cee 24ee 1cef 24ef
  //   1cf0 24f0 1cf1 24f1 1cf2 24f2 1cf3 24f3 1cf4 24f4 1cf5 24f5 1cf6 24f6 1cf7 24f7 1cf8 24f8 1cf9 24f9
  //   1cfa 24fa 1cfb 24fb 1cfc 24fc 1cfd 24fd 1cfe 24fe 1cff 24ff 200 2000 2001 2002 2003 2004 2005 2006
  //   2007 2008 2009 200a 200b 200c 200d 200e 200f 2010 2011 2012 2013 2014 2015 2016 2017 2018 2019 201a
  //   201b 201c 201d 201e 201f 2020 2021 2022 2023 2024 2025 2026 2027 2028 2029 202a 202b 202c 202d 202e
  //   202f 2030 2031 2032 2033 2034 2035 2036 2037 2038 2039 203a 203b 203c 203d 203e 203f 2040 2041 2042
  //   2043 2044 2045 2046 2047 2048 2049 204a 204b 204c 204d 204e 204f 2050 2051 2052 2053 2054 2055 2056
  //   2057 2058 2059 205a 205b 205c 205d 205e 205f 2060 2061 2062 2063 2064 2065 2066 2067 2068 2069 206a
  //   206b 206c 206d 206e 206f 2070 2071 2072 2073 2074 2075 2076 2077 2078 2079 207a 207b 207c 207d 207e
  //   207f 2080 2081 2082 2083 2084 2085 2086 2087 2088 2089 208a 208b 208c 208d 208e 208f 2090 2091 2092
  //   2093 2094 2095 2096 2097 2098 2099 209a 209b 209c 209d 209e 209f 20a0 20a1 20a2 20a3 20a4 20a5 20a6
  //   20a7 20a8 20a9 20aa 20ab 20ac 20ad 20ae 20af 20b0 20b1 20b2 20b3 20b4 20b5 20b6 20b7 20b8 20b9 20ba
  //   20bb 20bc 20bd 20be 20bf 20c0 20c1 20c2 20c3 20c4 20c5 20c6 20c7 20c8 20c9 20ca 20cb 20cc 20cd 20ce
  //   20cf 20d0 20d1 20d2 20d3 20d4 20d5 20d6 20d7 20d8 20d9 20da 20db 20dc 20dd 20de 20df 20e0 20e1 20e2
  //   20e3 20e4 20e5 20e6 20e7 20e8 20e9 20ea 20eb 20ec 20ed 20ee 20ef 20f0 20f1 20f2 20f3 20f4 20f5 20f6
  //   20f7 20f8 20f9 20fa 20fb 20fc 20fd 20fe 20ff 200 c000
endmodule

module RAM (
  input  [7:0] DBus_In,
  input  [8:0] RAMABus_In,
  input  [3:0] Page_in,
  input  LatchSafeDA,
  input  Clk,
  input  RESET,
  input  W,
  input  AsyncR_LatchSafeA,
  output [7:0] DBus_Out
);

  wire and_1_out, and_2_out, and_3_out, d_ff_1_q, d_ff_2_q, not_1_out, or_1_out, or_2_out;
  wire [7:0] controlled_buffer_1_out, register_1_q, register_2_q;

  Pull_Resistor pull_resistor_1 (.node(RAMABus_In[8]));
  not not_1 (not_1_out, RAMABus_In[8]);
  and and_1 (and_1_out, not_1_out, LatchSafeDA);
  and and_2 (and_2_out, W, not_1_out);
  and and_3 (and_3_out, AsyncR_LatchSafeA, not_1_out);
  or or_1 (or_1_out, and_1_out, and_3_out);
  Register register_1 (.D(DBus_In), .en(and_1_out), .Q(register_1_q), .clk(Clk), .clr(RESET));
  Register register_2 (.D(RAMABus_In[7:0]), .en(or_1_out), .Q(register_2_q), .clk(Clk), .clr(RESET));
  D_Flip_Flop d_ff_1 (.clk(Clk), .D(and_2_out), .Q(d_ff_1_q));  // open: Qn, preset, en, reset
  assign controlled_buffer_1_out = d_ff_2_q ? register_1_q : 8'bz;  // Controlled_Buffer controlled_buffer_1
  D_Flip_Flop d_ff_2 (.clk(Clk), .D(and_1_out), .Q(d_ff_2_q), .reset(RESET));  // open: Qn, preset, en
  or or_2 (or_2_out, d_ff_1_q, and_3_out);
  RAM_part #(.addrWidth(12), .bus("asynch")) ram_1 (
    .addr({Page_in, register_2_q}), .data(controlled_buffer_1_out), .sel(or_2_out), .ld(and_3_out),
    .clr(RESET));
  assign DBus_Out = and_3_out ? controlled_buffer_1_out : 8'bz;  // Controlled_Buffer controlled_buffer_2
endmodule

module PC (
  input  Latch_EN,
  input  [13:0] ROMABus_IN,
  input  INC_EN,
  input  CLK,
  input  RESET,
  input  CNDT_INC_EN,
  input  Conditional_Affirmative,
  output [13:0] PC_VAL
);

  wire and_1_out, or_1_out;

  or or_1 (or_1_out, INC_EN, and_1_out);
  and and_1 (and_1_out, CNDT_INC_EN, Conditional_Affirmative);
  Counter #(.width(14), .max('h3fff)) counter_1 (
    .load(Latch_EN), .D(ROMABus_IN), .count(or_1_out), .Q(PC_VAL), .clk(CLK), .clr(RESET));  // open: carry
endmodule

module Stack (
  input  [7:0] DATABUS_IN,
  input  Latch_Safe_Data,
  input  EN_DEC,
  input  EN_INC,
  input  CLK,
  input  RESET,
  input  Data_Out_Async,
  input  Data_In_Async,
  output [9:0] DBG,
  output [7:0] DATABUS_OUT
);

  wire d_ff_1_q, or_1_out;
  wire [7:0] controlled_buffer_1_out, register_1_q;

  Register register_1 (.D(DATABUS_IN), .en(Latch_Safe_Data), .Q(register_1_q), .clk(CLK), .clr(RESET));
  D_Flip_Flop d_ff_1 (.clk(CLK), .D(Latch_Safe_Data), .Q(d_ff_1_q), .reset(RESET));  // open: Qn, preset, en
  Counter #(.width(10), .max('h3ff)) counter_1 (
    .load(EN_DEC), .count(EN_INC), .Q(DBG), .clk(CLK), .clr(RESET));  // open: D, carry
  assign controlled_buffer_1_out = d_ff_1_q ? register_1_q : 8'bz;  // Controlled_Buffer controlled_buffer_1
  or or_1 (or_1_out, Data_In_Async, Data_Out_Async);
  RAM_part #(.addrWidth(10), .bus("asynch")) ram_1 (
    .addr(DBG), .data(controlled_buffer_1_out), .sel(or_1_out), .ld(Data_Out_Async), .clr(RESET));
  assign DATABUS_OUT = Data_Out_Async ? controlled_buffer_1_out : 8'bz;  // Controlled_Buffer controlled_buffer_2
endmodule

module RegA (
  input  [7:0] DBus_IN,
  input  LATCH_EN,
  input  CLK,
  input  RESET,
  input  OE,
  output [7:0] DBus_Out,
  output [7:0] Value
);

  Register register_1 (.D(DBus_IN), .en(LATCH_EN), .Q(Value), .clk(CLK), .clr(RESET));
  assign DBus_Out = OE ? Value : 8'bz;  // Controlled_Buffer controlled_buffer_1
endmodule

module RegB (
  input  [7:0] DBus_IN,
  input  LATCH_EN,
  input  CLK,
  input  RESET,
  input  OE,
  output [7:0] DBus_Out,
  output [7:0] Value
);

  Register register_1 (.D(DBus_IN), .en(LATCH_EN), .Q(Value), .clk(CLK), .clr(RESET));
  assign DBus_Out = OE ? Value : 8'bz;  // Controlled_Buffer controlled_buffer_1
endmodule

module Adr_Test (
  input  [8:0] Address_Is,
  input  [8:0] Address_Should,
  output out_3
);

  wire [8:0] xnor_1_out;

  Pull_Resistor pull_resistor_1 (.node(Address_Is));
  assign xnor_1_out = ~(Address_Is ^ Address_Should);  // XNOR_Gate xnor_1, 9 bits wide
  and and_1 (out_3, xnor_1_out[0], xnor_1_out[1], xnor_1_out[2], xnor_1_out[3], xnor_1_out[4], xnor_1_out[5], xnor_1_out[6], xnor_1_out[7], xnor_1_out[8]);
endmodule

module Page_Reg (
  input  [7:0] DBus_IN,
  input  RAM_W_Async,
  input  RAM_R_Async,
  input  [8:0] RAMABus_IN,
  input  CLK,
  input  RESET,
  output [7:0] DBG,
  output [7:0] DBus_Out,
  output [3:0] Ram_Page
);

  wire adr_test_1_out_3, and_1_out, and_2_out;

  and and_1 (and_1_out, adr_test_1_out_3, RAM_W_Async);
  and and_2 (and_2_out, RAM_R_Async, adr_test_1_out_3);
  Adr_Test adr_test_1 (.Address_Is(RAMABus_IN), .Address_Should(9'h101), .out_3(adr_test_1_out_3));
  Register #(.width(4)) register_1 (.D(DBus_IN[3:0]), .en(and_1_out), .Q(DBG[3:0]), .clk(CLK), .clr(RESET));
  assign DBus_Out = and_2_out ? {4'b0000, DBG[3:0]} : 8'bz;  // Controlled_Buffer controlled_buffer_1

  assign DBG[7:4] = 4'b0000;
  assign Ram_Page = DBG[3:0];
endmodule

module Status_Reg (
  input  [2:0] Comparison,
  input  [7:0] DBus_IN,
  input  RAM_W_Async,
  input  RAM_R_ASync,
  input  HBorrow_In,
  input  Sub_Latch_en,
  input  [8:0] RAMABus_IN,
  input  Borrow_In,
  input  HCarry_In,
  input  Add_Latch_EN,
  input  Carry_In,
  input  CLK,
  input  RESET,
  output ShiftIn,
  output [7:0] DBG,
  output [7:0] DBus_OUT
);

  wire adr_test_1_out_3, and_1_out, and_2_out;

  and and_1 (and_1_out, adr_test_1_out_3, RAM_W_Async);
  and and_2 (and_2_out, RAM_R_ASync, adr_test_1_out_3);
  Adr_Test adr_test_1 (.Address_Is(RAMABus_IN), .Address_Should(9'h100), .out_3(adr_test_1_out_3));
  D_Flip_Flop d_ff_1 (.clk(CLK), .D(DBus_IN[4]), .Q(DBG[4]), .en(and_1_out), .reset(RESET));  // open: Qn, preset
  D_Flip_Flop d_ff_2 (.clk(CLK), .D(HBorrow_In), .Q(DBG[3]), .en(Sub_Latch_en), .reset(RESET));  // open: Qn, preset
  D_Flip_Flop d_ff_3 (.clk(CLK), .D(Borrow_In), .Q(DBG[2]), .en(Sub_Latch_en), .reset(RESET));  // open: Qn, preset
  D_Flip_Flop d_ff_4 (.clk(CLK), .D(HCarry_In), .Q(DBG[1]), .en(Add_Latch_EN), .reset(RESET));  // open: Qn, preset
  D_Flip_Flop d_ff_5 (.clk(CLK), .D(Carry_In), .Q(DBG[0]), .en(Add_Latch_EN), .reset(RESET));  // open: Qn, preset
  assign DBus_OUT = and_2_out ? {Comparison, DBG[4:0]} : 8'bz;  // Controlled_Buffer controlled_buffer_1

  assign DBG[7:5] = Comparison;
  assign ShiftIn = DBG[4];
endmodule

module CrossOver (
  input  [15:0] Inst,
  input  Inst_0__7___DBus,
  output [7:0] DBus_Out
);

  assign DBus_Out = Inst_0__7___DBus ? Inst[7:0] : 8'bz;  // Controlled_Buffer controlled_buffer_1
endmodule

module Comparison (
  input  [7:0] A,
  input  [7:0] B,
  output [2:0] Comparison
);

  wire [7:0] xnor_1_out;

  assign xnor_1_out = ~(A ^ B);  // XNOR_Gate xnor_1, 8 bits wide
  nor nor_1 (Comparison[0], A[0], A[1], A[2], A[3], A[4], A[5], A[6], A[7]);
  nor nor_2 (Comparison[1], B[0], B[1], B[2], B[3], B[4], B[5], B[6], B[7]);
  and and_1 (Comparison[2], xnor_1_out[0], xnor_1_out[1], xnor_1_out[2], xnor_1_out[3], xnor_1_out[4], xnor_1_out[5], xnor_1_out[6], xnor_1_out[7]);
endmodule

module Control (
  input  [15:0] INST,
  input  DO_STEP_INST,
  input  BreakPoint,
  input  CLK,
  input  STEP_INST,
  input  RESET,
  output [7:0] DBG,
  output [7:0] CTRL_BUS_0,
  output [7:0] CTRL_BUS_1,
  output [7:0] CTRL_BUS_3,
  output [7:0] CTRL_BUS_4
);

  wire and_1_out, and_2_out, d_ff_1_q, d_ff_2_q, d_ff_3_q, d_ff_4_q, d_ff_5_q, not_1_out, not_2_out,
       not_3_out, or_1_out, or_2_out, or_3_out;

  D_Flip_Flop d_ff_1 (.clk(CLK), .D(CTRL_BUS_0[1]), .Q(d_ff_1_q), .en(or_1_out), .reset(RESET));  // open: Qn, preset
  or or_1 (or_1_out, CTRL_BUS_0[1], CTRL_BUS_0[6]);
  D_Flip_Flop d_ff_2 (.clk(CLK), .D(CTRL_BUS_0[0]), .Q(d_ff_2_q), .reset(RESET));  // open: Qn, preset, en
  D_Flip_Flop d_ff_3 (.clk(CLK), .D(CTRL_BUS_0[2]), .Q(d_ff_3_q), .reset(RESET));  // open: Qn, preset, en
  or or_2 (or_2_out, d_ff_1_q, DO_STEP_INST, BreakPoint, 1'b0);
  not not_1 (not_1_out, and_1_out);
  or or_3 (or_3_out, not_1_out, d_ff_5_q);
  ROM_part #(.addrWidth(7), .dataWidth(5)) rom_1 (.addr(INST[15:9]), .data(DBG[7:3]), .sel(1'b1));
  and and_1 (and_1_out, or_2_out, d_ff_3_q);
  not not_2 (not_2_out, d_ff_2_q);
  and and_2 (and_2_out, not_2_out, or_3_out);
  not not_3 (not_3_out, CLK);
  Counter #(.width(3), .max('h7)) counter_1 (
    .load(d_ff_2_q), .D(3'b000), .count(and_2_out), .Q(DBG[2:0]), .clk(not_3_out), .clr(RESET));  // open: carry
  D_Flip_Flop d_ff_4 (.clk(CLK), .D(CTRL_BUS_0[6]), .Q(d_ff_4_q), .reset(RESET));  // open: Qn, preset, en
  ROM_part rom_2 (.addr(DBG), .data(CTRL_BUS_0), .sel(1'b1));
  ROM_part rom_3 (.addr(DBG), .data(CTRL_BUS_1), .sel(1'b1));
  ROM_part rom_4 (.addr(DBG), .data(CTRL_BUS_3), .sel(1'b1));
  ROM_part rom_5 (.addr(DBG), .data(CTRL_BUS_4), .sel(1'b1));
  D_Flip_Flop d_ff_5 (.clk(STEP_INST), .D(1'b1), .Q(d_ff_5_q), .reset(d_ff_4_q));  // open: Qn, preset, en

  // Notes on the sheet:
  //   Reasons to Stop Execution:
  //   Sync Next + InstRLatch
  //   Next_Inst
  //   InstR_Latch_EN
  //   HALT
  //   HALT_CLEAR
  //   HALT
  //   Instruction Decode ROM
  //   Halt Instruction
  //   Make sure +1 is OFF
  //   when we load
  //   contents of rom_1 (hex, n*v repeats v):
  //   0 1 2 3 4 5 6 7 8 9 a b c d e f 10 11 12 13 4*14 8*0 16*15 16*16 32*17 32*18
  //   Halt only on step 0
  //   MicroCode  ROM 0
  //   MicroCode  ROM 1
  //   MicroCode  ROM 2
  //   MicroCode  ROM 3
  //   MicroCode  ROM 4
  //   contents of rom_2 (hex, n*v repeats v):
  //   4 49 6*0 4 b 6*0 4 40 0 9 4*0 4 40 0 9 4*0 4 48 1 5*0 4 40 0 0 21 0 0 0 4 49 6*0 4 49 6*0 4 49 6*0 4
  //   49 6*0 4 40 9 5*0 4 40 0 9 4*0 4 49 6*0 4 49 6*0 4 49 6*0 4 49 6*0 4 40 9 5*0 4 40 9 5*0 4 40 0 9
  //   4*0 4 40 0 9 4*0 4 49 6*0 4 48 11 5*0 4 48 11 5*0 4 48 5*0 21 44 21 61*0 55
  //   contents of rom_3 (hex, n*v repeats v):
  //   17*0 12 9 84 5*0 2 7*0 1 7*0 10 0 20 40 4*0 1 7*0 4 7*0 1 7*0 6 8*0 1 6*0 2 2 2 5*0 1 7*0 1 7*0 1
  //   7*0 4 8*0 1 7*0 4 6*0 2 2 2 5*0 8 8 8 5*0 1 8*0 2 84*0 55
  //   contents of rom_4 (hex, n*v repeats v):
  //   81*0 10 10 6*0 10 10 10 21*0 20 7*0 20 7*0 8 8 6*0 8 8 6*0 8 8 8 5*0 8 8 8 21*0 8 8 7*0 4 0 0 2 0 1
  //   0 1 61*0 55
  //   contents of rom_5 (hex, n*v repeats v):
  //   25*0 a0 20 28 5*0 10 40 6*0 10 40 10 40 36*0 2 2 6*0 4 5 4 37*0 2 2 6*0 2 2 6*0 4 5 4 5*0 4 5 4 21*0
  //   2 2 7*0 a0 28 20 a0 28 20 63*0 55
  //   Only Step on Rising Edge of Step Pulse
endmodule

module BitTest (
  input  [7:0] DBus_In,
  input  TestFor_1_0,
  input  [2:0] Bit,
  output Conditional_Affirmative
);

  wire [7:0] xnor_1_out;

  Pull_Resistor pull_resistor_1 (.node(DBus_In));
  assign xnor_1_out = ~(DBus_In ^ {8{TestFor_1_0}});  // XNOR_Gate xnor_1, 8 bits wide
  Multiplexer #(.select(3), .enable("false")) multiplexer_1 (
    .in0(xnor_1_out[0]), .in1(xnor_1_out[1]), .in2(xnor_1_out[2]), .in3(xnor_1_out[3]), .in4(xnor_1_out[4]),
    .in5(xnor_1_out[5]), .in6(xnor_1_out[6]), .in7(xnor_1_out[7]), .out(Conditional_Affirmative), .sel(Bit));
endmodule

module main (
);

  wire breakpoint_1_brkpt_triggered, CLK, clock_1_out, clockctrl_1_do_step_2, DO_STEP_CLK_out, Do_Step_Inst,
       DO_STEP_INST_out, Inst_Step, RST, STEP_CLK_out, undriven;
  wire [7:0] control_1_dbg, CTRLBus0, CTRLBus1, CTRLBus3, CTRLBus4, ram_1_dbus_out, rega_1_value;
  wire [13:0] inst_reg_1_inst_output, pc_1_pc_val;
  wire [15:0] rom_1_nextinst_out;
  wire [15:14] inst_reg_1_inst_output_2;

  // Probe on inst_reg_1_inst_output
  LED Conditioan_Affirmative (.in(undriven));
  LED Conditional_Inc (.in(CTRLBus0[4]));
  LED Latch_EN (.in(CTRLBus0[5]));
  LED INC_EN (.in(CTRLBus0[3]));
  LED LatchSafeDA_EN (.in(CTRLBus4[2]));
  LED RAM_R_Async (.in(CTRLBus4[1]));
  LED RAM_W_Async (.in(CTRLBus4[0]));
  // Probe on pc_1_pc_val
  PC pc_1 (
    .Latch_EN(CTRLBus0[5]), .ROMABus_IN(inst_reg_1_inst_output), .INC_EN(CTRLBus0[3]), .CLK(CLK),
    .RESET(RST), .PC_VAL(pc_1_pc_val), .CNDT_INC_EN(CTRLBus0[4]), .Conditional_Affirmative(undriven));
  RAM ram_1 (
    .RAMABus_In(inst_reg_1_inst_output[8:0]), .DBus_In(ram_1_dbus_out), .RESET(RST),
    .AsyncR_LatchSafeA(CTRLBus4[1]), .DBus_Out(ram_1_dbus_out), .Page_in(4'b0000), .LatchSafeDA(CTRLBus4[2]),
    .Clk(CLK), .W(CTRLBus4[0]));
  ROM rom_1 (.PC_VAL_IN(pc_1_pc_val), .NextInst_OUT(rom_1_nextinst_out));
  LED Latch_EN_2 (.in(CTRLBus0[2]));
  // Probe on ram_1_dbus_out
  // Probe on rega_1_value
  RegA rega_1 (
    .DBus_IN(ram_1_dbus_out), .LATCH_EN(CTRLBus1[0]), .CLK(CLK), .RESET(RST), .OE(CTRLBus1[1]),
    .DBus_Out(ram_1_dbus_out), .Value(rega_1_value));
  LED Latch_EN_3 (.in(CTRLBus1[0]));
  LED OE (.in(CTRLBus1[1]));
  BreakPoint breakpoint_1 (.ADR(pc_1_pc_val), .BRKPT_Triggered(breakpoint_1_brkpt_triggered));
  // Probe on {inst_reg_1_inst_output_2, inst_reg_1_inst_output}
  Inst_Reg inst_reg_1 (
    .NextInst_Input(rom_1_nextinst_out), .LATCH_EN(CTRLBus0[2]), .CLK(CLK), .RESET(RST),
    .Inst_Output({inst_reg_1_inst_output_2, inst_reg_1_inst_output}));
  LED Inst_0__7___DBus (.in(CTRLBus3[5]));
  // Probe on control_1_dbg
  Control control_1 (
    .CLK(CLK), .RESET(RST), .CTRL_BUS_0(CTRLBus0), .INST({inst_reg_1_inst_output_2, inst_reg_1_inst_output}),
    .CTRL_BUS_1(CTRLBus1), .CTRL_BUS_3(CTRLBus3), .CTRL_BUS_4(CTRLBus4), .DO_STEP_INST(Do_Step_Inst),
    .DBG(control_1_dbg), .BreakPoint(breakpoint_1_brkpt_triggered), .STEP_INST(Inst_Step));
  CrossOver crossover_1 (
    .Inst({inst_reg_1_inst_output_2, inst_reg_1_inst_output}), .DBus_Out(ram_1_dbus_out),
    .Inst_0__7___DBus(CTRLBus3[5]));
  Button u_DO_STEP_INST (.out(DO_STEP_INST_out));
  Button DO_STEP_CLK (.out(DO_STEP_CLK_out));
  LED led_1 (.in(clockctrl_1_do_step_2));
  Button STEP_CLK (.out(STEP_CLK_out));
  Button Reset (.out(RST));
  Button u_Inst_Step (.out(Inst_Step));
  LED led_2 (.in(Do_Step_Inst));
  Clock clock_1 (.out(clock_1_out));
  T_Flip_Flop t_ff_1 (.clk(DO_STEP_INST_out), .T(1'b1), .Q(Do_Step_Inst));  // open: Qn, preset, reset, en
  ClockCTRL clockctrl_1 (
    .MCLOCK_IN(clock_1_out), .Do_Step(DO_STEP_CLK_out), .Do_Step_2(clockctrl_1_do_step_2),
    .Step(STEP_CLK_out), .CLK(CLK), .Reset(RST));

  // Notes on the sheet:
  //   ROMABus:
  //   (hex)
  //   PC Val:
  //   (hex)
  //   Current Inst:
  //   Data Bus
  //   (hex)
  //   Val:
  //   (hex)
  //   (hex)
  //   InstCode+Step:
endmodule

// CLK
module ClockCTRL (
  input  MCLOCK_IN,
  input  Do_Step,
  input  Step,
  input  Reset,
  output CLK,
  output Do_Step_2
);

  wire and_1_out, d_ff_1_q, d_ff_1_qn, not_1_out, not_2_out, t_ff_1_qn, t_ff_2_q;

  T_Flip_Flop t_ff_1 (.clk(Do_Step), .T(1'b1), .Q(Do_Step_2), .Qn(t_ff_1_qn));  // open: preset, reset, en
  not not_1 (not_1_out, MCLOCK_IN);
  D_Flip_Flop d_ff_1 (
    .clk(not_1_out), .D(t_ff_1_qn), .Q(d_ff_1_q), .Qn(d_ff_1_qn), .en(not_2_out), .reset(Reset));  // open: preset
  T_Flip_Flop t_ff_2 (.clk(MCLOCK_IN), .T(d_ff_1_q), .Q(t_ff_2_q), .reset(Reset));  // open: Qn, preset, en
  not not_2 (not_2_out, t_ff_2_q);
  and and_1 (and_1_out, d_ff_1_qn, Step);
  or or_1 (CLK, t_ff_2_q, and_1_out);
endmodule

module BreakPoint (
  input  [13:0] ADR,
  output BRKPT_Triggered
);

  wire and_1_out, and_2_out, rom_adr_test_1_out_3, rom_adr_test_2_out_3;

  ROM_Adr_Test rom_adr_test_1 (.Address_Is(14'h4), .Address_Should(ADR), .out_3(rom_adr_test_1_out_3));
  ROM_Adr_Test rom_adr_test_2 (.Address_Is(14'h9), .Address_Should(ADR), .out_3(rom_adr_test_2_out_3));
  and and_1 (and_1_out, rom_adr_test_1_out_3, 1'b0);
  and and_2 (and_2_out, rom_adr_test_2_out_3, 1'b0);
  or or_1 (BRKPT_Triggered, and_1_out, and_2_out);

  // Notes on the sheet:
  //   Break at adr:
  //   Enable Breakpoint:
  //   Break at adr:
  //   Enable Breakpoint:
endmodule

module ROM_Adr_Test (
  input  [13:0] Address_Is,
  input  [13:0] Address_Should,
  output out_3
);

  wire [13:0] xnor_1_out;

  Pull_Resistor pull_resistor_1 (.node(Address_Is));
  assign xnor_1_out = ~(Address_Is ^ Address_Should);  // XNOR_Gate xnor_1, 14 bits wide
  // Probe on xnor_1_out
  and and_1 (out_3, xnor_1_out[0], xnor_1_out[1], xnor_1_out[2], xnor_1_out[3], xnor_1_out[4], xnor_1_out[5], xnor_1_out[6], xnor_1_out[7], xnor_1_out[8], xnor_1_out[9], xnor_1_out[10], xnor_1_out[11], xnor_1_out[12], xnor_1_out[13]);
endmodule
